// Logisim project Microprocessor.circ as structural Verilog
module AND_1 (
  input  AX,
  input  BX,
  input  CX,
  input  DX,
  input  EX,
  input  DR,
  input  IR,
  input  AX__DR,
  input  BX__DR,
  input  CX__DR,
  input  DX__DR,
  input  EX__DR,
  input  AX__IR,
  input  BX__IR,
  input  CX__IR,
  input  DX__IR,
  input  EX__IR,
  input  AX__BX,
  input  AX__CX,
  input  AX__DX,
  input  AX__EX,
  input  BX__CX,
  input  BX__DX,
  input  BX__EX,
  input  CX__DX,
  input  CX__EX,
  input  DX__EX,
  output OUTPUT
);

  wire and_1_out, and_2_out, and_3_out, and_4_out, and_5_out, and_6_out, and_7_out, and_8_out, and_9_out,
       and_10_out, and_11_out, and_12_out, and_13_out, and_14_out, and_15_out, and_16_out, and_17_out,
       and_18_out, and_19_out, and_20_out;

  and and_1 (and_1_out, AX__DR, DR, AX);
  and and_2 (and_2_out, BX__DR, DR, BX);
  and and_3 (and_3_out, CX__DR, DR, CX);
  and and_4 (and_4_out, DX__DR, DR, DX);
  and and_5 (and_5_out, EX__DR, DR, EX);
  and and_6 (and_6_out, AX__IR, IR, AX);
  and and_7 (and_7_out, BX__IR, IR, BX);
  and and_8 (and_8_out, CX__IR, IR, CX);
  and and_9 (and_9_out, DX__IR, IR, DX);
  and and_10 (and_10_out, EX__IR, IR, EX);
  and and_11 (and_11_out, AX__BX, BX, AX);
  and and_12 (and_12_out, AX__CX, CX, AX);
  and and_13 (and_13_out, AX__DX, DX, AX);
  and and_14 (and_14_out, AX__EX, EX, AX);
  and and_15 (and_15_out, BX__CX, CX, BX);
  and and_16 (and_16_out, BX__DX, DX, BX);
  and and_17 (and_17_out, BX__EX, EX, BX);
  and and_18 (and_18_out, CX__DX, DX, CX);
  and and_19 (and_19_out, CX__EX, EX, CX);
  and and_20 (and_20_out, DX__EX, EX, CX);
  or or_1 (OUTPUT, and_1_out, and_2_out, and_3_out, and_4_out, and_5_out, and_6_out, and_7_out, and_8_out, and_9_out, and_10_out, and_11_out, and_12_out, and_13_out, and_14_out, and_15_out, and_16_out, and_17_out, and_18_out, and_19_out, and_20_out);
endmodule
